# Fritzing sketch Embedded Micro Mojo v3 test sketch (saved by Fritzing 0.9.3b)
circuit board: 8.46667cm x 7cm

parts:
  Mojo1 = Embedded Micro Mojo v3
  J2 = female pin header, 5 pins [form="♀ (female)"]
  J1 = female pin header, 5 pins [form="♀ (female)"]
  J3 = female pin header, 25 pins [form="♀ (female)"]
  J4 = female pin header, 25 pins [form="♀ (female)"]
  J5 = female pin header, 25 pins [form="♀ (female)"]
  J6 = female pin header, 25 pins [form="♀ (female)"]

nets:
  N1: Mojo1.GND, J2.pin1, J3.pin1, J3.pin2, J5.pin1, J5.pin2, J6.pin25
  N2: Mojo1.RAW, J4.pin1, J6.pin1
  N3: Mojo1.V+, J4.pin2, J6.pin2
  N4: Mojo1.SUS, J5.pin3
  N5: Mojo1.DONE, J6.pin3
  N6: Mojo1.58, J5.pin4
  N7: Mojo1.57, J6.pin4
  N8: Mojo1.67, J5.pin5
  N9: Mojo1.66, J6.pin5
  N10: Mojo1.75, J5.pin6
  N11: Mojo1.74, J6.pin6
  N12: Mojo1.79, J5.pin7
  N13: Mojo1.78, J6.pin7
  N14: Mojo1.81, J5.pin8
  N15: Mojo1.80, J6.pin8
  N16: Mojo1.83, J5.pin9
  N17: Mojo1.82, J6.pin9
  N18: Mojo1.85, J5.pin10
  N19: Mojo1.84, J6.pin10
  N20: Mojo1.88, J5.pin11
  N21: Mojo1.87, J6.pin11
  N22: Mojo1.93, J5.pin12
  N23: Mojo1.92, J6.pin12
  N24: Mojo1.95, J5.pin13
  N25: Mojo1.94, J6.pin13
  N26: Mojo1.98, J5.pin14
  N27: Mojo1.97, J6.pin14
  N28: Mojo1.100, J5.pin15
  N29: Mojo1.99, J6.pin15
  N30: Mojo1.102, J5.pin16
  N31: Mojo1.101, J6.pin16
  N32: Mojo1.105, J5.pin17
  N33: Mojo1.104, J6.pin17
  N34: Mojo1.112, J5.pin18
  N35: Mojo1.111, J6.pin18
  N36: Mojo1.115, J5.pin19
  N37: Mojo1.114, J6.pin19
  N38: Mojo1.117, J5.pin20
  N39: Mojo1.116, J6.pin20
  N40: Mojo1.119, J5.pin21
  N41: Mojo1.118, J6.pin21
  N42: Mojo1.121, J5.pin22
  N43: Mojo1.120, J6.pin22
  N44: Mojo1.TMS, J5.pin23
  N45: Mojo1.TDO, J6.pin23
  N46: Mojo1.TDI, J5.pin24
  N47: Mojo1.TCK, J6.pin24
  N48: Mojo1.RST, J5.pin25
  N49: Mojo1.51, J3.pin3
  N50: Mojo1.50, J4.pin3
  N51: Mojo1.41, J3.pin4
  N52: Mojo1.40, J4.pin4
  N53: Mojo1.35, J3.pin5
  N54: Mojo1.34, J4.pin5
  N55: Mojo1.33, J3.pin6
  N56: Mojo1.32, J4.pin6
  N57: Mojo1.30, J3.pin7
  N58: Mojo1.29, J4.pin7
  N59: Mojo1.27, J3.pin8
  N60: Mojo1.26, J4.pin8
  N61: Mojo1.24, J3.pin9
  N62: Mojo1.23, J4.pin9
  N63: Mojo1.22, J3.pin10
  N64: Mojo1.21, J4.pin10
  N65: Mojo1.17, J3.pin11
  N66: Mojo1.16, J4.pin11
  N67: Mojo1.15, J3.pin12
  N68: Mojo1.14, J4.pin12
  N69: Mojo1.12, J3.pin13
  N70: Mojo1.11, J4.pin13
  N71: Mojo1.10, J3.pin14
  N72: Mojo1.9, J4.pin14
  N73: Mojo1.8, J3.pin15
  N74: Mojo1.7, J4.pin15
  N75: Mojo1.6, J3.pin16
  N76: Mojo1.5, J4.pin16
  N77: Mojo1.2, J3.pin17
  N78: Mojo1.1, J4.pin17
  N79: Mojo1.144, J3.pin18
  N80: Mojo1.143, J4.pin18
  N81: Mojo1.142, J3.pin19
  N82: Mojo1.141, J4.pin19
  N83: Mojo1.140, J3.pin20
  N84: Mojo1.139, J4.pin20
  N85: Mojo1.138, J3.pin21
  N86: Mojo1.137, J4.pin21
  N87: Mojo1.134, J3.pin22
  N88: Mojo1.133, J4.pin22
  N89: Mojo1.132, J3.pin23
  N90: Mojo1.131, J4.pin23
  N91: Mojo1.127, J3.pin24
  N92: Mojo1.126, J4.pin24
  N93: Mojo1.124, J3.pin25
  N94: Mojo1.123, J4.pin25
  N95: Mojo1.AREF, J1.pin1
  N96: Mojo1.A8, J2.pin2
  N97: Mojo1.A9, J1.pin2
  N98: Mojo1.A6, J2.pin3
  N99: Mojo1.A7, J1.pin3
  N100: Mojo1.A4, J2.pin4
  N101: Mojo1.A5, J1.pin4
  N102: Mojo1.A0, J2.pin5
  N103: Mojo1.A1, J1.pin5

custom parts:
  Embedded Micro Mojo v3: The Mojo is a FPGA development board that is designed from the ground up to be easy to use. The entire goal of the Mojo is to make getting started with FPGA and digital design as easy as possible. To go along with our board, Embedded Micro has tutorials to help you get started and expand your knowledge of digital design. The Mojo is made in the USA. The Mojo features include: Spartan 6 XC6SLX9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
